// Logisim project control-logic.circ as structural Verilog: 1 circuit, main circuit control_logic
module control_logic (
  input  [31:0] Instruction,
  input  BrEq,
  input  BrLt,
  output PCSel,
  output RegWEn,
  output [2:0] ImmSel,
  output BrUn,
  output ASel,
  output BSel,
  output [3:0] ALUSel,
  output MemWEn,
  output [1:0] WBSel
);

  wire and_1_out, and_2_out, and_3_out, and_4_out, comparator_10_eq, comparator_11_eq, comparator_12_eq,
       comparator_13_eq, comparator_14_eq, comparator_15_eq, comparator_16_eq, comparator_17_eq,
       demultiplexer_1_out2, demultiplexer_2_out2, demultiplexer_6_out1, demultiplexer_6_out2, is_add,
       is_addi, is_and, is_andi, is_auipc, is_bge, is_bgeu, is_blt, is_bltu, is_bne, is_branch, is_breq,
       is_itype, is_jal, is_jalr, is_lb, is_lh, is_load, is_lui, is_lw, is_mul, is_mulh, is_mulhu, is_or,
       is_ori, is_rtype, is_sb, is_sh, is_sll, is_slli, is_slt, is_slti, is_sra, is_srai, is_srl, is_srli,
       is_store, is_sub, is_sw, is_xor, is_xori, not_1_out, not_2_out, or_1_out, or_2_out, or_3_out,
       or_4_out, or_5_out, or_6_out, or_7_out;
  wire [2:0] InstructionType;
  wire [5:0] ROMIn;
  wire [6:0] multiplexer_1_out, multiplexer_2_out, multiplexer_3_out, multiplexer_4_out;
  wire [15:14] rom_1_data;

  ROM #(.addrWidth(6), .dataWidth(16)) rom_1 (
    .addr(ROMIn), .data({rom_1_data, WBSel, MemWEn, ALUSel, BSel, ASel, BrUn, ImmSel, RegWEn}));
  Priority_Encoder #(.select_enc(6)) priority_encoder_1 (
    .in0(is_add), .in1(is_mul), .in2(is_sub), .in3(is_sll), .in4(is_mulh), .in5(is_mulhu), .in6(is_slt),
    .in7(is_xor), .in8(is_srl), .in9(is_sra), .in10(is_or), .in11(is_and), .in12(is_lb), .in13(is_lh),
    .in14(is_lw), .in15(is_addi), .in16(is_slli), .in17(is_slti), .in18(is_xori), .in19(is_srli),
    .in20(is_srai), .in21(is_ori), .in22(is_andi), .in23(is_sb), .in24(is_sh), .in25(is_sw), .in26(is_breq),
    .in27(is_bne), .in28(is_blt), .in29(is_bge), .in30(is_bltu), .in31(is_bgeu), .in32(is_auipc),
    .in33(is_lui), .in34(is_jal), .in35(is_jalr), .out(ROMIn));  // open: in36, in37, in38, in39, in40, in41, in42, in43, in44, in45, in46, in47, in48, in49, in50, in51, in52, in53, in54, in55, in56, in57, in58, in59, in60, in61, in62, in63, gs, en_out, en_in
  Priority_Encoder priority_encoder_2 (
    .in0(is_branch), .in1(is_itype), .in2(is_rtype), .in3(is_load), .in4(is_store), .in5(is_lui),
    .in6(is_auipc), .out(InstructionType));  // open: in7, en_in, gs, en_out
  Comparator #(.mode("unsigned"), .width(5)) comparator_1 (
    .a(Instruction[6:2]), .b(5'b11000), .eq(is_branch));  // open: gt, lt
  Comparator #(.mode("unsigned"), .width(5)) comparator_2 (
    .a(Instruction[6:2]), .b(5'b00100), .eq(is_itype));  // open: gt, lt
  Comparator #(.mode("unsigned"), .width(5)) comparator_3 (
    .a(Instruction[6:2]), .b(5'b01100), .eq(is_rtype));  // open: gt, lt
  Comparator #(.mode("unsigned"), .width(5)) comparator_4 (
    .a(Instruction[6:2]), .b({5{1'b0}}), .eq(is_load));  // open: gt, lt
  Comparator #(.mode("unsigned"), .width(5)) comparator_5 (
    .a(Instruction[6:2]), .b(5'b01000), .eq(is_store));  // open: gt, lt
  Comparator #(.mode("unsigned"), .width(5)) comparator_6 (
    .a(Instruction[6:2]), .b(5'b11011), .eq(is_jal));  // open: gt, lt
  Comparator #(.mode("unsigned"), .width(5)) comparator_7 (
    .a(Instruction[6:2]), .b(5'b11001), .eq(is_jalr));  // open: gt, lt
  Comparator #(.mode("unsigned"), .width(5)) comparator_8 (
    .a(Instruction[6:2]), .b(5'b00101), .eq(is_auipc));  // open: gt, lt
  Comparator #(.mode("unsigned"), .width(5)) comparator_9 (
    .a(Instruction[6:2]), .b(5'b01101), .eq(is_lui));  // open: gt, lt
  or or_1 (or_1_out, is_blt, is_bltu);
  not not_1 (not_1_out, BrLt);
  and and_1 (and_1_out, BrEq, is_breq);
  or or_2 (or_2_out, BrEq, not_1_out);
  or or_3 (or_3_out, is_bge, is_bgeu);
  not not_2 (not_2_out, BrEq);
  and and_2 (and_2_out, BrLt, or_1_out);
  and and_3 (and_3_out, or_2_out, or_3_out);
  and and_4 (and_4_out, not_2_out, is_bne);
  Comparator #(.width(3)) comparator_10 (.a(Instruction[14:12]), .b(3'b000), .eq(comparator_10_eq));  // open: gt, lt
  Comparator #(.width(3)) comparator_11 (.a(Instruction[14:12]), .b(3'b001), .eq(comparator_11_eq));  // open: gt, lt
  Comparator #(.width(3)) comparator_12 (.a(Instruction[14:12]), .b(3'b101), .eq(comparator_12_eq));  // open: gt, lt
  Comparator #(.width(3)) comparator_13 (.a(Instruction[14:12]), .b(3'b110), .eq(comparator_13_eq));  // open: gt, lt
  or or_4 (or_4_out, and_1_out, and_2_out);
  Demultiplexer #(.select(3)) demultiplexer_1 (
    .out0(is_breq), .out1(is_addi), .out2(demultiplexer_1_out2), .out3(is_lb), .out4(is_sb),
    .in(comparator_10_eq), .sel(InstructionType));  // open: out5, out6, out7
  Demultiplexer #(.select(3)) demultiplexer_2 (
    .out0(is_bne), .out1(is_slli), .out2(demultiplexer_2_out2), .out3(is_lh), .out4(is_sh),
    .in(comparator_11_eq), .sel(InstructionType));  // open: out5, out6, out7
  Comparator #(.width(3)) comparator_14 (.a(Instruction[14:12]), .b(3'b010), .eq(comparator_14_eq));  // open: gt, lt
  Comparator #(.width(3)) comparator_15 (.a(Instruction[14:12]), .b(3'b100), .eq(comparator_15_eq));  // open: gt, lt
  Comparator #(.width(3)) comparator_16 (.a(Instruction[14:12]), .b(3'b111), .eq(comparator_16_eq));  // open: gt, lt
  Demultiplexer #(.select(3)) demultiplexer_3 (
    .out1(is_slti), .out2(is_slt), .out3(is_lw), .out4(is_sw), .in(comparator_14_eq), .sel(InstructionType));  // open: out0, out5, out6, out7
  Demultiplexer #(.select(3)) demultiplexer_4 (
    .out2(is_mulhu), .in(comparator_17_eq), .sel(InstructionType));  // open: out0, out1, out3, out4, out5, out6, out7
  Comparator #(.width(3)) comparator_17 (.a(Instruction[14:12]), .b(3'b011), .eq(comparator_17_eq));  // open: gt, lt
  Demultiplexer #(.select(3)) demultiplexer_5 (
    .out0(is_blt), .out1(is_xori), .out2(is_xor), .in(comparator_15_eq), .sel(InstructionType));  // open: out3, out4, out5, out6, out7
  Demultiplexer #(.select(3)) demultiplexer_6 (
    .out0(is_bge), .out1(demultiplexer_6_out1), .out2(demultiplexer_6_out2), .in(comparator_12_eq),
    .sel(InstructionType));  // open: out3, out4, out5, out6, out7
  Demultiplexer #(.select(3)) demultiplexer_7 (
    .out0(is_bltu), .out1(is_ori), .out2(is_or), .in(comparator_13_eq), .sel(InstructionType));  // open: out3, out4, out5, out6, out7
  Demultiplexer #(.select(3)) demultiplexer_8 (
    .out0(is_bgeu), .out1(is_andi), .out2(is_and), .in(comparator_16_eq), .sel(InstructionType));  // open: out3, out4, out5, out6, out7
  or or_5 (or_5_out, or_4_out, and_3_out);
  or or_6 (or_6_out, or_5_out, and_4_out);
  or or_7 (or_7_out, is_jal, is_jalr);
  or or_8 (PCSel, or_6_out, or_7_out);
  Multiplexer #(.width(7)) multiplexer_1 (
    .in0({7{1'b1}}), .in1(Instruction[31:25]), .out(multiplexer_1_out), .sel(demultiplexer_1_out2));
  Comparator #(.width(7)) comparator_18 (.a(multiplexer_1_out), .b({7{1'b0}}), .eq(is_add));  // open: gt, lt
  Multiplexer #(.width(7)) multiplexer_2 (
    .in0({7{1'b1}}), .in1(Instruction[31:25]), .out(multiplexer_2_out), .sel(demultiplexer_2_out2));
  Multiplexer #(.width(7)) multiplexer_3 (
    .in0({7{1'b1}}), .in1(Instruction[31:25]), .out(multiplexer_3_out), .sel(demultiplexer_6_out2));
  Comparator #(.width(7)) comparator_19 (.a(multiplexer_2_out), .b(7'b0000001), .eq(is_mulh));  // open: gt, lt
  Multiplexer #(.width(7)) multiplexer_4 (
    .in0({7{1'b1}}), .in1(Instruction[31:25]), .out(multiplexer_4_out), .sel(demultiplexer_6_out1));
  Comparator #(.width(7)) comparator_20 (.a(multiplexer_3_out), .b(7'b0100000), .eq(is_sra));  // open: gt, lt
  Comparator #(.width(7)) comparator_21 (.a(multiplexer_1_out), .b(7'b0000001), .eq(is_mul));  // open: gt, lt
  Comparator #(.width(7)) comparator_22 (.a(multiplexer_2_out), .b({7{1'b0}}), .eq(is_sll));  // open: gt, lt
  Comparator #(.width(7)) comparator_23 (.a(multiplexer_4_out), .b(7'b0100000), .eq(is_srai));  // open: gt, lt
  Comparator #(.width(7)) comparator_24 (.a(multiplexer_3_out), .b({7{1'b0}}), .eq(is_srl));  // open: gt, lt
  Comparator #(.width(7)) comparator_25 (.a(multiplexer_1_out), .b(7'b0100000), .eq(is_sub));  // open: gt, lt
  Comparator #(.width(7)) comparator_26 (.a(multiplexer_4_out), .b({7{1'b0}}), .eq(is_srli));  // open: gt, lt

  // Other names for the same wires on the sheet: opcode[4:0] = Instruction[6:2]; funct3[2:0] = Instruction[14:12];
  //   funct7[6:0] = Instruction[31:25]

  // Notes on the sheet:
  //   INPUTS to your circuit
  //   Connect ROM Input here ->
  //   contents of rom_1 (hex, n*v repeats v):
  //   1001 1401 1601 1081 1481 1581 1101 1201 1281 1681 1301 1381 41 41 41 1041 10cf 1141 1241 12cf 16cf
  //   1341 13c1 3842 3842 3842 4*3064 3074 3074 1067 17c7 2069 2041
  //   ROM FOR CONTROL LOGIC
  //   DON'T CHANGE THE LOCATIONS OF THE INPUTS AND OUTPUTS!
  //   This is only if you choose to do the ROM option
  //   CONNECT
  //   WIRE
  //   TO
  //   USE
  //   ROM
  //   OUTPUT from your circuit
  //   Reminder: If using ROM, use combinational logic for PCSel
endmodule
