// Logisim project cpu.circ as structural Verilog: 1 circuit, main circuit cpu
module cpu (
  input  clk,
  input  [31:0] Instruction,
  input  [31:0] MemReadData,
  output [31:0] MemAddress,
  output [31:0] ProgramCounter,
  output [31:0] ra,
  output [31:0] sp,
  output [31:0] t0,
  output [31:0] t1,
  output [31:0] t2,
  output [31:0] s0,
  output [31:0] s1,
  output [31:0] a0,
  output [3:0] MemWriteMask,
  output [31:0] MemWriteData
);

  wire ASel, BrEq, BrLt, BrUn, BSel, MemWEn, PCSel, RegWEn;
  wire [1:0] WBSel;
  wire [2:0] func3, ImmSel;
  wire [3:0] ALUSel;
  wire [4:0] Imm;
  wire [6:0] funct7, opcode;
  wire [19:7] pipelinedInstruction;
  wire [31:0] adder_1_out, adder_2_out, Immediate, multiplexer_1_out, multiplexer_2_out, multiplexer_3_out,
       multiplexer_4_out, pipelinedALU, pipelinedPC, readdata, ReadData1, ReadData2, register_4_q, undriven,
       WriteData;

  Adder #(.width(32)) adder_1 (.a(ProgramCounter), .b(32'h4), .out(adder_1_out));  // open: cin, cout
  Multiplexer #(.width(32)) multiplexer_1 (.in0(Instruction), .in1(undriven), .out(multiplexer_1_out), .sel(PCSel));
  Multiplexer #(.width(32)) multiplexer_2 (.in0(adder_1_out), .in1(MemAddress), .out(multiplexer_2_out), .sel(PCSel));
  Register #(.width(32)) PC (.D(multiplexer_2_out), .en(1'b1), .clk(clk), .Q(ProgramCounter));  // open: clr
  Register #(.width(32)) register_1 (
    .D(multiplexer_1_out), .en(1'b1), .clk(clk),
    .Q({funct7, Imm, pipelinedInstruction[19:15], func3, pipelinedInstruction[11:7], opcode}));  // open: clr
  Register #(.width(32)) register_2 (.D(ProgramCounter), .en(1'b1), .clk(clk), .Q(pipelinedPC));  // open: clr
  Register #(.width(32)) register_3 (.D(MemAddress), .en(1'b1), .clk(clk), .Q(pipelinedALU));  // open: clr
  control_logic control_logic_1 (
    .Instruction({funct7, Imm, pipelinedInstruction[19:15], func3, pipelinedInstruction[11:7], opcode}),
    .BrEq(BrEq), .BrLt(BrLt), .PCSel(PCSel), .RegWEn(RegWEn), .ImmSel(ImmSel), .BrUn(BrUn), .ASel(ASel),
    .BSel(BSel), .ALUSel(ALUSel), .MemWEn(MemWEn), .WBSel(WBSel));
  regfile regfile_1 (
    .ReadIndex1(pipelinedInstruction[19:15]), .ReadIndex2(Imm), .WriteIndex(pipelinedInstruction[11:7]),
    .WriteData(WriteData), .RegWEn(RegWEn), .clk(clk), .ra(ra), .sp(sp), .t0(t0), .t1(t1), .t2(t2), .s0(s0),
    .s1(s1), .a0(a0), .ReadData1(ReadData1), .ReadData2(ReadData2));
  imm_gen imm_gen_1 (
    .Instruction({funct7, Imm, pipelinedInstruction[19:15], func3, pipelinedInstruction[11:7], opcode}),
    .ImmSel(ImmSel), .Immediate(Immediate));
  Multiplexer #(.width(32)) multiplexer_3 (.in0(ReadData1), .in1(pipelinedPC), .out(multiplexer_3_out), .sel(ASel));
  Multiplexer #(.width(32)) multiplexer_4 (.in0(ReadData2), .in1(Immediate), .out(multiplexer_4_out), .sel(BSel));
  alu alu_1 (.A(multiplexer_3_out), .B(multiplexer_4_out), .ALUSel(ALUSel), .ALUResult(MemAddress));
  branch_comp branch_comp_1 (.BrData1(ReadData1), .BrData2(ReadData2), .BrUn(BrUn), .BrEq(BrEq), .BrLt(BrLt));
  Adder #(.width(32)) adder_2 (.a(ProgramCounter), .b(32'h4), .out(adder_2_out));  // open: cin, cout
  partial_load partial_load_1 (
    .Instruction({funct7, Imm, pipelinedInstruction[19:15], func3, pipelinedInstruction[11:7], opcode}),
    .MemAddress(MemAddress), .DataFromMem(MemReadData), .DataToReg(readdata));
  Register #(.width(32)) register_4 (.D(adder_2_out), .en(1'b1), .clk(clk), .Q(register_4_q));  // open: clr
  Multiplexer #(.select(2), .width(32)) multiplexer_5 (
    .in0(readdata), .in1(MemAddress), .in2(register_4_q), .out(WriteData), .sel(WBSel));  // open: in3
  partial_store partial_store_1 (
    .Instruction({funct7, Imm, pipelinedInstruction[19:15], func3, pipelinedInstruction[11:7], opcode}),
    .MemAddress(MemAddress), .DataFromReg(ReadData2), .MemWEn(MemWEn), .MemWriteMask(MemWriteMask),
    .DataToMem(MemWriteData));

  // Other names for the same wires on the sheet: aluResult[31:0] = MemAddress;
  //   pipelinedInstruction (some bits) = {funct7, Imm, func3, opcode}; opcodeMSB[4:0] = opcode[6:2];
  //   rd[4:0] = pipelinedInstruction[11:7]; rs1[4:0] = pipelinedInstruction[19:15]; rs2[4:0] = Imm;
  //   Imm[11:5] = funct7

  // Notes on the sheet:
  //   To IMEM
  //   IMEM (do **NOT** move this)
  //   From IMEM
  //   Inputs/Outputs for testing. Do **NOT** move these.
  //   It is OK to move the PC, RegFile, ALU, MEM, Branch Comp, Imm Gen, Partial Load, Partial Store and Control Logic to wherever is most convenient for you when constructing your CPU, and to delete this text
  //   To DMEM
  //   DMEM (do **NOT** move this)
  //   From DMEM
endmodule
