// Logisim project imm-gen.circ as structural Verilog: 1 circuit, main circuit imm_gen
module imm_gen (
  input  [31:0] Instruction,
  input  [2:0] ImmSel,
  output [31:0] Immediate
);

  wire [31:5] imm_Istar;
  wire [31:11] imm_I, imm_S;
  wire [31:13] imm_B;
  wire [31:20] imm_J;

  Multiplexer #(.width(21)) multiplexer_1 (.in0({21{1'b0}}), .in1({21{1'b1}}), .out(imm_I), .sel(Instruction[31]));
  Multiplexer #(.width(27)) multiplexer_2 (.in0({27{1'b0}}), .in1({27{1'b1}}), .out(imm_Istar), .sel(Instruction[24]));
  Multiplexer #(.width(19)) multiplexer_3 (.in0({19{1'b0}}), .in1({19{1'b1}}), .out(imm_B), .sel(Instruction[31]));
  Multiplexer #(.width(21)) multiplexer_4 (.in0({21{1'b0}}), .in1({21{1'b1}}), .out(imm_S), .sel(Instruction[31]));
  Multiplexer #(.width(12)) multiplexer_5 (.in0({12{1'b0}}), .in1({12{1'b1}}), .out(imm_J), .sel(Instruction[31]));
  Multiplexer #(.select(3), .width(32)) multiplexer_6 (
    .in0({imm_I, Instruction[30:20]}), .in1({imm_S, Instruction[30:25], Instruction[11:7]}),
    .in2({imm_B, Instruction[31], Instruction[7], Instruction[30:25], Instruction[11:8], 1'b0}),
    .in3({Instruction[31:12], {12{1'b0}}}),
    .in4({imm_J, Instruction[19:12], Instruction[20], Instruction[30:21], 1'b0}),
    .in7({imm_Istar, Instruction[24:20]}), .out(Immediate), .sel(ImmSel));  // open: in5, in6

  // Other names for the same wires on the sheet: imm_B[12:1] = {Instruction[31], Instruction[7], Instruction[30:25], Instruction[11:8]};
  //   imm_U[31:12] = Instruction[31:12]; imm_I[10:0] = Instruction[30:20]; imm_Istar[4:0] = Instruction[24:20];
  //   imm_J[19:1] = {Instruction[19:12], Instruction[20], Instruction[30:21]};
  //   imm_S[10:0] = {Instruction[30:25], Instruction[11:7]}

  // Notes on the sheet:
  //   INPUTS to your circuit
  //   DON'T CHANGE THE LOCATIONS OF THE INPUTS AND OUTPUTS!
  //   OUTPUT from your circuit
endmodule
