// Logisim project partial-load.circ as structural Verilog: 1 circuit, main circuit partial_load
module partial_load (
  input  [31:0] Instruction,
  input  [31:0] MemAddress,
  input  [31:0] DataFromMem,
  output [31:0] DataToReg
);

  wire comparator_1_eq, comparator_2_eq, comparator_3_eq, comparator_4_eq, comparator_5_eq, comparator_6_eq,
       comparator_10_eq, comparator_11_eq, is_lb, is_lb00, is_lb01, is_lb10, is_lb11, is_lh, is_lh00,
       is_lh01, is_lh10, is_lw, is_lw00;
  wire [2:0] scenario;
  wire [31:8] input0, input1, input2, input3;
  wire [31:16] input4, input5, input6;

  Comparator #(.width(2)) comparator_1 (.a(MemAddress[1:0]), .b(2'b00), .eq(comparator_1_eq));  // open: gt, lt
  Comparator #(.width(2)) comparator_2 (.a(MemAddress[1:0]), .b(2'b10), .eq(comparator_2_eq));  // open: gt, lt
  Comparator #(.width(2)) comparator_3 (.a(MemAddress[1:0]), .b(2'b11), .eq(comparator_3_eq));  // open: gt, lt
  Comparator #(.width(2)) comparator_4 (.a(MemAddress[1:0]), .b(2'b01), .eq(comparator_4_eq));  // open: gt, lt
  Comparator #(.width(2)) comparator_5 (.a(MemAddress[1:0]), .b(2'b10), .eq(comparator_5_eq));  // open: gt, lt
  Comparator #(.width(2)) comparator_6 (.a(MemAddress[1:0]), .b(2'b00), .eq(comparator_6_eq));  // open: gt, lt
  Comparator #(.width(3)) comparator_7 (.a(Instruction[14:12]), .b(3'b000), .eq(is_lb));  // open: gt, lt
  Comparator #(.width(3)) comparator_8 (.a(Instruction[14:12]), .b(3'b001), .eq(is_lh));  // open: gt, lt
  Comparator #(.width(3)) comparator_9 (.a(Instruction[14:12]), .b(3'b010), .eq(is_lw));  // open: gt, lt
  Comparator #(.width(2)) comparator_10 (.a(MemAddress[1:0]), .b(2'b01), .eq(comparator_10_eq));  // open: gt, lt
  Comparator #(.width(2)) comparator_11 (.a(MemAddress[1:0]), .b(2'b00), .eq(comparator_11_eq));  // open: gt, lt
  and and_1 (is_lb00, comparator_1_eq, is_lb);
  and and_2 (is_lb01, comparator_10_eq, is_lb);
  and and_3 (is_lb10, comparator_2_eq, is_lb);
  and and_4 (is_lb11, comparator_3_eq, is_lb);
  and and_5 (is_lh00, comparator_11_eq, is_lh);
  and and_6 (is_lh01, comparator_4_eq, is_lh);
  and and_7 (is_lh10, comparator_5_eq, is_lh);
  and and_8 (is_lw00, comparator_6_eq, is_lw);
  Multiplexer #(.width(24)) multiplexer_1 (.in0({24{1'b0}}), .in1({24{1'b1}}), .out(input0), .sel(DataFromMem[7]));
  Multiplexer #(.select(3), .width(32)) multiplexer_2 (
    .in0({input0, DataFromMem[7:0]}), .in1({input1, DataFromMem[15:8]}), .in2({input2, DataFromMem[23:16]}),
    .in3({input3, DataFromMem[31:24]}), .in4({input4, DataFromMem[15:0]}), .in5({input5, DataFromMem[23:8]}),
    .in6({input6, DataFromMem[31:16]}), .in7(DataFromMem), .out(DataToReg), .sel(scenario));
  Priority_Encoder priority_encoder_1 (
    .in0(is_lb00), .in1(is_lb01), .in2(is_lb10), .in3(is_lb11), .in4(is_lh00), .in5(is_lh01), .in6(is_lh10),
    .in7(is_lw00), .out(scenario));  // open: en_in, gs, en_out
  Multiplexer #(.width(24)) multiplexer_3 (.in0({24{1'b0}}), .in1({24{1'b1}}), .out(input1), .sel(DataFromMem[15]));
  Multiplexer #(.width(24)) multiplexer_4 (.in0({24{1'b0}}), .in1({24{1'b1}}), .out(input2), .sel(DataFromMem[23]));
  Multiplexer #(.width(24)) multiplexer_5 (.in0({24{1'b0}}), .in1({24{1'b1}}), .out(input3), .sel(DataFromMem[31]));
  Multiplexer #(.width(16)) multiplexer_6 (.in0({16{1'b0}}), .in1({16{1'b1}}), .out(input4), .sel(DataFromMem[15]));
  Multiplexer #(.width(16)) multiplexer_7 (.in0({16{1'b0}}), .in1({16{1'b1}}), .out(input5), .sel(DataFromMem[23]));
  Multiplexer #(.width(16)) multiplexer_8 (.in0({16{1'b0}}), .in1({16{1'b1}}), .out(input6), .sel(DataFromMem[31]));

  // Other names for the same wires on the sheet: input0[7:0] = DataFromMem[7:0]; input4[15:0] = DataFromMem[15:0];
  //   input1[7:0] = DataFromMem[15:8]; input5[15:0] = DataFromMem[23:8]; input2[7:0] = DataFromMem[23:16];
  //   input6[15:0] = DataFromMem[31:16]; input3[7:0] = DataFromMem[31:24]; funct3[2:0] = Instruction[14:12];
  //   bottom2bits[1:0] = MemAddress[1:0]

  // Notes on the sheet:
  //   INPUTS to your circuit
  //   DON'T CHANGE THE LOCATIONS OF THE INPUTS AND OUTPUTS!
  //   OUTPUT from your circuit
endmodule
