// Logisim project partial-store.circ as structural Verilog: 1 circuit, main circuit partial_store
module partial_store (
  input  [31:0] Instruction,
  input  [31:0] MemAddress,
  input  [31:0] DataFromReg,
  input  MemWEn,
  output [3:0] MemWriteMask,
  output [31:0] DataToMem
);

  wire comparator_4_eq, comparator_5_eq, comparator_6_eq, comparator_7_eq, comparator_8_eq, comparator_9_eq,
       comparator_10_eq, is_sb, is_sb00, is_sb01, is_sb10, is_sb11, is_sh, is_sh00, is_sh01, is_sw, is_sw00;
  wire [2:0] scenario;
  wire [3:0] mwm;

  Comparator #(.width(3)) comparator_1 (.a(Instruction[14:12]), .b(3'b000), .eq(is_sb));  // open: gt, lt
  Comparator #(.width(3)) comparator_2 (.a(Instruction[14:12]), .b(3'b001), .eq(is_sh));  // open: gt, lt
  Comparator #(.width(3)) comparator_3 (.a(Instruction[14:12]), .b(3'b010), .eq(is_sw));  // open: gt, lt
  Comparator #(.width(2)) comparator_4 (.a(MemAddress[1:0]), .b(2'b00), .eq(comparator_4_eq));  // open: gt, lt
  Comparator #(.width(2)) comparator_5 (.a(MemAddress[1:0]), .b(2'b01), .eq(comparator_5_eq));  // open: gt, lt
  Comparator #(.width(2)) comparator_6 (.a(MemAddress[1:0]), .b(2'b10), .eq(comparator_6_eq));  // open: gt, lt
  Comparator #(.width(2)) comparator_7 (.a(MemAddress[1:0]), .b(2'b11), .eq(comparator_7_eq));  // open: gt, lt
  Comparator #(.width(2)) comparator_8 (.a(MemAddress[1:0]), .b(2'b00), .eq(comparator_8_eq));  // open: gt, lt
  Comparator #(.width(2)) comparator_9 (.a(MemAddress[1:0]), .b(2'b10), .eq(comparator_9_eq));  // open: gt, lt
  Comparator #(.width(2)) comparator_10 (.a(MemAddress[1:0]), .b(2'b00), .eq(comparator_10_eq));  // open: gt, lt
  and and_1 (is_sb00, comparator_4_eq, is_sb);
  and and_2 (is_sb01, comparator_5_eq, is_sb);
  and and_3 (is_sb10, comparator_6_eq, is_sb);
  and and_4 (is_sb11, comparator_7_eq, is_sb);
  and and_5 (is_sh00, comparator_8_eq, is_sh);
  and and_6 (is_sh01, comparator_9_eq, is_sh);
  and and_7 (is_sw00, comparator_10_eq, is_sw);
  Priority_Encoder priority_encoder_1 (
    .in0(is_sb00), .in1(is_sb01), .in2(is_sb10), .in3(is_sb11), .in4(is_sh00), .in5(is_sh01), .in7(is_sw00),
    .out(scenario));  // open: in6, en_in, gs, en_out
  Multiplexer #(.width(4)) multiplexer_1 (.in0(4'b0000), .in1(mwm), .out(MemWriteMask), .sel(MemWEn));
  Multiplexer #(.select(3), .width(32)) multiplexer_2 (
    .in0({{24{1'b0}}, DataFromReg[7:0]}), .in1({{16{1'b0}}, DataFromReg[7:0], {8{1'b0}}}),
    .in2({{8{1'b0}}, DataFromReg[7:0], {16{1'b0}}}), .in3({DataFromReg[7:0], {24{1'b0}}}),
    .in4({{16{1'b0}}, DataFromReg[15:0]}), .in5({DataFromReg[15:0], {16{1'b0}}}), .in7(DataFromReg),
    .out(DataToMem), .sel(scenario));  // open: in6
  Multiplexer #(.select(3), .width(4)) multiplexer_3 (
    .in0(4'b0001), .in1(4'b0010), .in2(4'b0100), .in3(4'b1000), .in4(4'b0011), .in5(4'b1100), .in7(4'b1111),
    .out(mwm), .sel(scenario));  // open: in6

  // Other names for the same wires on the sheet: input0[7:0] = DataFromReg[7:0]; input1[15:8] = DataFromReg[7:0];
  //   input2[23:16] = DataFromReg[7:0]; input3[31:24] = DataFromReg[7:0]; input4[15:0] = DataFromReg[15:0];
  //   input5[31:16] = DataFromReg[15:0]; funct3[2:0] = Instruction[14:12]; bottom2bits[1:0] = MemAddress[1:0]

  // Notes on the sheet:
  //   INPUTS to your circuit
  //   DON'T CHANGE THE LOCATIONS OF THE INPUTS AND OUTPUTS!
  //   OUTPUT from your circuit
endmodule
