// Logisim project regfile.circ as structural Verilog: 1 circuit, main circuit regfile
module regfile (
  input  [4:0] ReadIndex1,
  input  [4:0] ReadIndex2,
  input  [4:0] WriteIndex,
  input  [31:0] WriteData,
  input  RegWEn,
  input  clk,
  output [31:0] ra,
  output [31:0] sp,
  output [31:0] t0,
  output [31:0] t1,
  output [31:0] t2,
  output [31:0] s0,
  output [31:0] s1,
  output [31:0] a0,
  output [31:0] ReadData1,
  output [31:0] ReadData2
);

  wire demultiplexer_2_out0, x1w, x2w, x3w, x4w, x5w, x6w, x7w, x8w, x9w, x10w, x11w, x12w, x13w, x14w, x15w,
       x16w, x17w, x18w, x19w, x20w, x21w, x22w, x23w, x24w, x25w, x26w, x27w, x28w, x29w, x30w, x31w;
  wire [31:0] demultiplexer_1_out0, x0out, x1, x2, x3, x3out, x4, x4out, x5, x6, x7, x8, x9, x10, x11,
       x11out, x12, x12out, x13, x13out, x14, x14out, x15, x15out, x16, x16out, x17, x17out, x18, x18out,
       x19, x19out, x20, x20out, x21, x21out, x22, x22out, x23, x23out, x24, x24out, x25, x25out, x26,
       x26out, x27, x27out, x28, x28out, x29, x29out, x30, x30out, x31, x31out;

  Register #(.width(32)) x0 (.D({32{1'b0}}), .en(1'b0), .clk(clk), .Q(x0out));  // open: clr
  Register #(.width(32)) u_x1 (.D(x1), .en(x1w), .clk(clk), .Q(ra));  // open: clr
  Register #(.width(32)) u_x2 (.D(x2), .en(x2w), .clk(clk), .Q(sp));  // open: clr
  Register #(.width(32)) u_x3 (.D(x3), .en(x3w), .clk(clk), .Q(x3out));  // open: clr
  Register #(.width(32)) u_x4 (.D(x4), .en(x4w), .clk(clk), .Q(x4out));  // open: clr
  Register #(.width(32)) u_x5 (.D(x5), .en(x5w), .clk(clk), .Q(t0));  // open: clr
  Register #(.width(32)) u_x6 (.D(x6), .en(x6w), .clk(clk), .Q(t1));  // open: clr
  Register #(.width(32)) u_x7 (.D(x7), .en(x7w), .clk(clk), .Q(t2));  // open: clr
  Register #(.width(32)) u_x8 (.D(x8), .en(x8w), .clk(clk), .Q(s0));  // open: clr
  Register #(.width(32)) u_x9 (.D(x9), .en(x9w), .clk(clk), .Q(s1));  // open: clr
  Register #(.width(32)) u_x11 (.D(x11), .en(x11w), .clk(clk), .Q(x11out));  // open: clr
  Register #(.width(32)) u_x10 (.D(x10), .en(x10w), .clk(clk), .Q(a0));  // open: clr
  Register #(.width(32)) u_x12 (.D(x12), .en(x12w), .clk(clk), .Q(x12out));  // open: clr
  Register #(.width(32)) u_x13 (.D(x13), .en(x13w), .clk(clk), .Q(x13out));  // open: clr
  Register #(.width(32)) u_x14 (.D(x14), .en(x14w), .clk(clk), .Q(x14out));  // open: clr
  Register #(.width(32)) u_x30 (.D(x30), .en(x30w), .clk(clk), .Q(x30out));  // open: clr
  Register #(.width(32)) u_x15 (.D(x15), .en(x15w), .clk(clk), .Q(x15out));  // open: clr
  Register #(.width(32)) u_x16 (.D(x16), .en(x16w), .clk(clk), .Q(x16out));  // open: clr
  Register #(.width(32)) u_x17 (.D(x17), .en(x17w), .clk(clk), .Q(x17out));  // open: clr
  Register #(.width(32)) u_x18 (.D(x18), .en(x18w), .clk(clk), .Q(x18out));  // open: clr
  Register #(.width(32)) u_x19 (.D(x19), .en(x19w), .clk(clk), .Q(x19out));  // open: clr
  Register #(.width(32)) u_x20 (.D(x20), .en(x20w), .clk(clk), .Q(x20out));  // open: clr
  Register #(.width(32)) u_x21 (.D(x21), .en(x21w), .clk(clk), .Q(x21out));  // open: clr
  Register #(.width(32)) u_x22 (.D(x22), .en(x22w), .clk(clk), .Q(x22out));  // open: clr
  Register #(.width(32)) u_x24 (.D(x24), .en(x24w), .clk(clk), .Q(x24out));  // open: clr
  Register #(.width(32)) u_x23 (.D(x23), .en(x23w), .clk(clk), .Q(x23out));  // open: clr
  Register #(.width(32)) u_x25 (.D(x25), .en(x25w), .clk(clk), .Q(x25out));  // open: clr
  Register #(.width(32)) u_x26 (.D(x26), .en(x26w), .clk(clk), .Q(x26out));  // open: clr
  Register #(.width(32)) u_x27 (.D(x27), .en(x27w), .clk(clk), .Q(x27out));  // open: clr
  Register #(.width(32)) u_x28 (.D(x28), .en(x28w), .clk(clk), .Q(x28out));  // open: clr
  Register #(.width(32)) u_x29 (.D(x29), .en(x29w), .clk(clk), .Q(x29out));  // open: clr
  Register #(.width(32)) u_x31 (.D(x31), .en(x31w), .clk(clk), .Q(x31out));  // open: clr
  Demultiplexer #(.select(5), .width(32)) demultiplexer_1 (
    .out0(demultiplexer_1_out0), .out1(x1), .out2(x2), .out3(x3), .out4(x4), .out5(x5), .out6(x6), .out7(x7),
    .out8(x8), .out9(x9), .out10(x10), .out11(x11), .out12(x12), .out13(x13), .out14(x14), .out15(x15),
    .out16(x16), .out17(x17), .out18(x18), .out19(x19), .out20(x20), .out21(x21), .out22(x22), .out23(x23),
    .out24(x24), .out25(x25), .out26(x26), .out27(x27), .out28(x28), .out29(x29), .out30(x30), .out31(x31),
    .in(WriteData), .sel(WriteIndex));
  Multiplexer #(.select(5), .width(32)) multiplexer_1 (
    .in0(x0out), .in1(ra), .in2(sp), .in3(x3out), .in4(x4out), .in5(t0), .in6(t1), .in7(t2), .in8(s0),
    .in9(s1), .in10(a0), .in11(x11out), .in12(x12out), .in13(x13out), .in14(x14out), .in15(x15out),
    .in16(x16out), .in17(x17out), .in18(x18out), .in19(x19out), .in20(x20out), .in21(x21out), .in22(x22out),
    .in23(x23out), .in24(x24out), .in25(x25out), .in26(x26out), .in27(x27out), .in28(x28out), .in29(x29out),
    .in30(x30out), .in31(x31out), .out(ReadData2), .sel(ReadIndex2));
  Multiplexer #(.select(5), .width(32)) multiplexer_2 (
    .in0(x0out), .in1(ra), .in2(sp), .in3(x3out), .in4(x4out), .in5(t0), .in6(t1), .in7(t2), .in8(s0),
    .in9(s1), .in10(a0), .in11(x11out), .in12(x12out), .in13(x13out), .in14(x14out), .in15(x15out),
    .in16(x16out), .in17(x17out), .in18(x18out), .in19(x19out), .in20(x20out), .in21(x21out), .in22(x22out),
    .in23(x23out), .in24(x24out), .in25(x25out), .in26(x26out), .in27(x27out), .in28(x28out), .in29(x29out),
    .in30(x30out), .in31(x31out), .out(ReadData1), .sel(ReadIndex1));
  Demultiplexer #(.select(5)) demultiplexer_2 (
    .out0(demultiplexer_2_out0), .out1(x1w), .out2(x2w), .out3(x3w), .out4(x4w), .out5(x5w), .out6(x6w),
    .out7(x7w), .out8(x8w), .out9(x9w), .out10(x10w), .out11(x11w), .out12(x12w), .out13(x13w), .out14(x14w),
    .out15(x15w), .out16(x16w), .out17(x17w), .out18(x18w), .out19(x19w), .out20(x20w), .out21(x21w),
    .out22(x22w), .out23(x23w), .out24(x24w), .out25(x25w), .out26(x26w), .out27(x27w), .out28(x28w),
    .out29(x29w), .out30(x30w), .out31(x31w), .in(RegWEn), .sel(WriteIndex));

  // Other names for the same wires on the sheet: x1out[31:0] = ra; x2out[31:0] = sp; x5out[31:0] = t0;
  //   x6out[31:0] = t1; x7out[31:0] = t2; x8out[31:0] = s0; x9out[31:0] = s1; x10out[31:0] = a0

  // Notes on the sheet:
  //   INPUTS to your circuit
  //   DON'T CHANGE THE LOCATIONS OF THE INPUTS AND OUTPUTS!
  //   These are DEBUG/TEST outputs from your circuit.
  //   OUTPUTS from your circuit
endmodule
